# Fritzing sketch fishfeeder (saved by Fritzing 0.9.3b)
circuit board: 3.24137cm x 2.62042cm
breadboards: 1

parts:
  SW = female pin header, 2 pins [form="♀ (female)"]
  M = female pin header, 2 pins [form="♀ (female)"]
  D1R = female pin header, 8 pins [form="♀ (female)"]
  1k = Resistor [tolerance=±5% resistance=1k package=THT]
  100k = Resistor [tolerance=±5% resistance=100k package=THT]
  D1L = female pin header, 8 pins [form="♀ (female)"]
  Q1 = NPN-Transistor [package="TO92 [THT]"]

nets:
  N1: SW.pin1, M.pin2, D1L.pin8
  N2: SW.pin2, 100k.Pin_0, D1L.pin5
  N3: M.pin1, Q1.E
  N4: D1R.pin7, 1k.Pin_0, 100k.Pin_1, Q1.C
  N5: 1k.Pin_1, D1L.pin4, Q1.B
